// Digital circuit ALU.dig as structural Verilog
module ALU (
  input  [3:0] A,
  input  [3:0] B,
  input  Sel0,
  input  Sel1,
  input  Sel2,
  output Zero,
  output [3:0] Result
);

  wire [3:0] fourbitand_1_r0, fourbitor_1_r3, fourbitxor_1_r0, rcaddersubtractor_1_r0;

  fourBitOR fourbitor_1 (
    .B0(B[0]), .A0(A[0]), .A1(A[1]), .A2(A[2]), .A3(A[3]), .B1(B[1]), .B2(B[2]), .B3(B[3]),
    .R0(fourbitor_1_r3[0]), .R1(fourbitor_1_r3[1]), .R2(fourbitor_1_r3[2]), .R3(fourbitor_1_r3[3]));
  rcAdderSubtractor rcaddersubtractor_1 (
    .A0(A[0]), .A1(A[1]), .A2(A[2]), .A3(A[3]), .B0(B[0]), .B1(B[1]), .B2(B[2]), .B3(B[3]), .Sub(Sel0),
    .R0(rcaddersubtractor_1_r0[0]), .R1(rcaddersubtractor_1_r0[1]), .R2(rcaddersubtractor_1_r0[2]),
    .R3(rcaddersubtractor_1_r0[3]));  // open: Co
  fourBitAND fourbitand_1 (
    .B0(B[0]), .B1(B[1]), .B2(B[2]), .B3(B[3]), .A0(A[0]), .A1(A[1]), .A2(A[2]), .A3(A[3]),
    .R0(fourbitand_1_r0[0]), .R1(fourbitand_1_r0[1]), .R2(fourbitand_1_r0[2]), .R3(fourbitand_1_r0[3]));
  fourBitXOR fourbitxor_1 (
    .B0(B[0]), .B1(B[1]), .B2(B[2]), .B3(B[3]), .A0(A[0]), .A1(A[1]), .A2(A[2]), .A3(A[3]),
    .R0(fourbitxor_1_r0[0]), .R1(fourbitxor_1_r0[1]), .R2(fourbitxor_1_r0[2]), .R3(fourbitxor_1_r0[3]));
  Multiplexer #(.Selector_Bits(3), .Bits(4)) multiplexer_1 (
    .sel({Sel2, Sel1, Sel0}), .in_0(rcaddersubtractor_1_r0), .in_1(rcaddersubtractor_1_r0),
    .in_2(fourbitand_1_r0), .in_3(fourbitor_1_r3), .in_4(fourbitxor_1_r0), .in_5(4'b0000), .in_6(4'b0000),
    .in_7(4'b0000), .out(Result));
  fourBitZero fourbitzero_1 (.A0(Result[0]), .A1(Result[1]), .A2(Result[2]), .A3(Result[3]), .R0(Zero));
endmodule

/* Test case ALUtest:
Sel2 Sel1 Sel0  A3 A2 A1 A0 B3 B2 B1 B0 R3 R2 R1 R0

# OR Tests (Sel = 011)
loop(A,16)
  loop(B,16)
 0 1 1 bits(4,A) bits(4,B) bits(4,A | B)
  end loop
end loop

# ADD Tests (Sel = 000, Sub=0)
loop(A,16)
  loop(B,16)
0 0 0 bits(4,A) bits(4,B) bits(4,A+B)
  end loop
end loop

# SUB Tests (Sel = 001, Sub=1)
loop(A,16)
  loop(B,16)
0 0 1 bits(4,A) bits(4,B) bits(4,A-B)
  end loop
end loop

# AND Tests (Sel = 010)
loop(A,16)
  loop(B,16)
 0 1 0 bits(4,A) bits(4,B) bits(4,A&B)
  end loop
end loop

# XOR Tests (Sel = 100) 
loop(A,16)
  loop(B,16)
 1 0 0 bits(4,A) bits(4,B) bits(4,A^B)
  end loop
end loop
*/
