// Digital circuit control_unit.dig as structural Verilog
module control_unit (
  input  [1:0] Op,
  output [2:0] ALUOp,
  output RegWrite
);


  assign ALUOp = {1'b0, Op};
  assign RegWrite = 1'b1;
endmodule
