// Digital circuit fourBitAND.dig as structural Verilog
module fourBitAND (
  input  B0,
  input  B1,
  input  B2,
  input  B3,
  input  A0,
  input  A1,
  input  A2,
  input  A3,
  output R0,
  output R1,
  output R2,
  output R3
);

  and and_1 (R3, A3, B3);
  and and_2 (R2, A2, B2);
  and and_3 (R1, A1, B1);
  and and_4 (R0, A0, B0);
endmodule

/* Test case AndTest:
A3 A2 A1 A0 B3 B2 B1 B0 R3 R2 R1 R0
loop(A,16)
loop(B,16)
	 bits(4,A) bits(4,B) bits(4, A&B)
end loop
end loop
*/
