// Digital circuit fourBitOR.dig as structural Verilog
module fourBitOR (
  input  B0,
  input  A0,
  input  A1,
  input  A2,
  input  A3,
  input  B1,
  input  B2,
  input  B3,
  output R0,
  output R1,
  output R2,
  output R3
);

  or or_1 (R3, B3, A3);
  or or_2 (R2, B2, A2);
  or or_3 (R1, B1, A1);
  or or_4 (R0, B0, A0);
endmodule

/* Test case ORTester:
A3 A2 A1 A0 B3 B2 B1 B0 R3 R2 R1 R0
loop(A,16)
loop(B,16)
	 bits(4,A) bits(4,B) bits(4, A|B)
end loop
end loop
*/
