// Digital circuit fourBitXOR.dig as structural Verilog
module fourBitXOR (
  input  B0,
  input  B1,
  input  B2,
  input  B3,
  input  A0,
  input  A1,
  input  A2,
  input  A3,
  output R0,
  output R1,
  output R2,
  output R3
);

  xor xor_1 (R3, A3, B3);
  xor xor_2 (R2, A2, B2);
  xor xor_3 (R1, A1, B1);
  xor xor_4 (R0, A0, B0);
endmodule
