// Digital circuit fourBitZero.dig as structural Verilog
module fourBitZero (
  input  A0,
  input  A1,
  input  A2,
  input  A3,
  output R0
);

  wire nor_1_out, nor_2_out;

  nor nor_1 (nor_1_out, A0, A1);
  nor nor_2 (nor_2_out, A2, A3);
  and and_1 (R0, nor_1_out, nor_2_out);
endmodule

/* Test case ZeroTest:
# Zero Detector Tests
A3 A2 A1 A0 R0
0 0 0 0 1
0 0 0 1 0
0 0 1 0 0
0 0 1 1 0
0 1 0 0 0
0 1 0 1 0
0 1 1 0 0
0 1 1 1 0
1 0 0 0 0
1 0 0 1 0
1 0 1 0 0
1 0 1 1 0
1 1 0 0 0
1 1 0 1 0
1 1 1 0 0
1 1 1 1 0
*/
