// Digital circuit fullAdder.dig as structural Verilog
module fullAdder (
  input  A,
  input  B,
  input  Cin,
  output Sum,
  output Out
);

  wire halfadder_1_c0, halfadder_1_s0, halfadder_2_c0;

  halfAdder halfadder_1 (.A0(B), .B0(Cin), .S0(halfadder_1_s0), .C0(halfadder_1_c0));
  halfAdder halfadder_2 (.A0(A), .B0(halfadder_1_s0), .S0(Sum), .C0(halfadder_2_c0));
  or or_1 (Out, halfadder_2_c0, halfadder_1_c0);
endmodule
