// Digital circuit fullAdderSubtractor.dig as structural Verilog
module fullAdderSubtractor (
  input  A,
  input  Sub,
  input  B,
  output S,
  output Co
);

  wire xor_1_out;

  xor xor_1 (xor_1_out, Sub, B);
  fullAdder fulladder_1 (.A(A), .B(xor_1_out), .Cin(Sub), .Sum(S), .Out(Co));
endmodule
