// Digital circuit instruction_decoder.dig as structural Verilog
module instruction_decoder (
  input  [7:0] Instruction,
  output [1:0] Op,
  output [2:0] RegA,
  output [2:0] RegB
);


  assign Op = Instruction[7:6];
  assign RegA = Instruction[5:3];
  assign RegB = Instruction[2:0];
endmodule
