// Digital circuit instruction_memory.dig as structural Verilog
module instruction_memory (
  input  [5:0] Address,
  output [7:0] Instruction
);

  ROM #(.AddrBits(6), .Bits(8)) Instruction_Memory (.A(Address), .sel(1'b1), .D(Instruction));

  // Notes on the sheet:
  //   contents of Instruction_Memory (hex, n*v repeats v):
  //   0,a,53,ae,f7
endmodule
