// Digital circuit main_cpu.dig as structural Verilog
module main_cpu (
  input  Clock,
  input  Reset,
  input  TestClock,
  input  TestMode,
  input  [2:0] TestWriteReg,
  input  [3:0] TestWriteData,
  input  TestRegWrite,
  output [7:0] Instruction,
  output [1:0] Op,
  output [2:0] RegA,
  output [2:0] RegB
);

  wire alu_1_zero, control_unit_1_regwrite, multiplexer_1_out, multiplexer_4_out;
  wire [2:0] control_unit_1_aluop, multiplexer_2_out;
  wire [3:0] alu_1_result, multiplexer_3_out, register_file_1_readdata1, register_file_1_readdata2;
  wire [5:0] pc_unit_1_pc;

  pc_unit pc_unit_1 (.Clock(Clock), .Reset(Reset), .PC(pc_unit_1_pc));
  Multiplexer multiplexer_1 (.sel(TestMode), .in_0(Clock), .in_1(TestClock), .out(multiplexer_1_out));
  instruction_memory instruction_memory_1 (.Address(pc_unit_1_pc), .Instruction(Instruction));
  Multiplexer #(.Bits(3)) multiplexer_2 (.sel(TestMode), .in_0(RegA), .in_1(TestWriteReg), .out(multiplexer_2_out));
  Multiplexer #(.Bits(4)) multiplexer_3 (
    .sel(TestMode), .in_0(alu_1_result), .in_1(TestWriteData), .out(multiplexer_3_out));
  Multiplexer multiplexer_4 (
    .sel(TestMode), .in_0(control_unit_1_regwrite), .in_1(TestRegWrite), .out(multiplexer_4_out));
  instruction_decoder instruction_decoder_1 (.Instruction(Instruction), .Op(Op), .RegA(RegA), .RegB(RegB));
  register_file register_file_1 (
    .ReadReg1(multiplexer_2_out), .ReadReg2(RegB), .WriteReg(multiplexer_2_out),
    .WriteData(multiplexer_3_out), .RegWrite(multiplexer_4_out), .Clock(multiplexer_1_out),
    .ReadData1(register_file_1_readdata1), .ReadData2(register_file_1_readdata2));
  control_unit control_unit_1 (.Op(Op), .ALUOp(control_unit_1_aluop), .RegWrite(control_unit_1_regwrite));
  ALU alu_1 (
    .A(register_file_1_readdata1), .B(register_file_1_readdata2), .Sel0(control_unit_1_aluop[0]),
    .Sel1(control_unit_1_aluop[1]), .Sel2(control_unit_1_aluop[2]), .Zero(alu_1_zero), .Result(alu_1_result));
  LED led_1 (.in(alu_1_zero));
  Seven_Seg_Hex seven_seg_hex_1 (.d(alu_1_result), .dp(1'b1));
  Seven_Seg_Hex seven_seg_hex_2 (.d(register_file_1_readdata1), .dp(1'b1));
  Seven_Seg_Hex seven_seg_hex_3 (.d(register_file_1_readdata2), .dp(1'b1));
endmodule
