// Digital circuit pc_unit.dig as structural Verilog
module pc_unit (
  input  Clock,
  input  Reset,
  output [5:0] PC
);

  CounterPreset #(.maxValue(16), .Bits(6)) u_PC (
    .en(1'b1), .C(Clock), .dir(1'b0), .in({6{1'b0}}), .ld(Reset), .clr(1'b0), .out(PC));  // open: ovf
endmodule
