// Digital circuit rcAdder.dig as structural Verilog
module rcAdder (
  input  Ci,
  input  B0,
  input  B1,
  input  B2,
  input  A0,
  input  A1,
  input  A2,
  input  B3,
  input  A3,
  output S0,
  output S1,
  output S2,
  output C0,
  output S3
);

  wire fulladder_2_out, fulladder_3_out, fulladder_4_out;

  fullAdder fulladder_1 (.A(A3), .B(B3), .Cin(fulladder_2_out), .Sum(S3), .Out(C0));
  fullAdder fulladder_2 (.A(A2), .B(B2), .Cin(fulladder_3_out), .Sum(S2), .Out(fulladder_2_out));
  fullAdder fulladder_3 (.A(A1), .B(B1), .Cin(fulladder_4_out), .Sum(S1), .Out(fulladder_3_out));
  fullAdder fulladder_4 (.A(A0), .B(B0), .Cin(Ci), .Sum(S0), .Out(fulladder_4_out));
endmodule

/* Test case rcAdderTest:
Ci A3 A2 A1 A0 B3 B2 B1 B0 C0 S3 S2 S1 S0
loop (A, 16)
	loop(B, 16)
	0 bits(4,A) bits(4, B) bits(5, A+B)
	1 bits(4,A) bits(4, B) bits(5, A+B+1)
	end loop	
end loop
*/
