// Digital circuit rcAdderSubtractor.dig as structural Verilog
module rcAdderSubtractor (
  input  A0,
  input  A1,
  input  A2,
  input  A3,
  input  B0,
  input  B1,
  input  B2,
  input  B3,
  input  Sub,
  output R0,
  output R1,
  output R2,
  output R3,
  output Co
);

  wire fourbitxor_1_r0, fourbitxor_1_r1, fourbitxor_1_r2, fourbitxor_1_r3;

  fourBitXOR fourbitxor_1 (
    .B0(B0), .B1(B1), .B2(B2), .B3(B3), .A0(Sub), .A1(Sub), .A2(Sub), .A3(Sub), .R0(fourbitxor_1_r0),
    .R1(fourbitxor_1_r1), .R2(fourbitxor_1_r2), .R3(fourbitxor_1_r3));
  rcAdder rcadder_1 (
    .Ci(Sub), .B0(fourbitxor_1_r0), .B1(fourbitxor_1_r1), .B2(fourbitxor_1_r2), .A0(A0), .A1(A1), .A2(A2),
    .B3(fourbitxor_1_r3), .A3(A3), .S0(R0), .S1(R1), .S2(R2), .C0(Co), .S3(R3));
endmodule

/* Test case rcAdderSubTest:
            Sub   A3 A2 A1 A0  B3 B2 B1 B0  R3 R2 R1 R0
loop(A,16)
  loop(B,16)
0 bits(4,A) bits(4,B) bits(4,A+B)
1 bits(4,A) bits(4,B) bits(4,A-B)
  end loop
end loop
*/
