// Digital circuit register_file.dig as structural Verilog
module register_file (
  input  [2:0] ReadReg1,
  input  [2:0] ReadReg2,
  input  [2:0] WriteReg,
  input  [3:0] WriteData,
  input  RegWrite,
  input  Clock,
  output [3:0] ReadData1,
  output [3:0] ReadData2
);

  wire and_1_out, and_2_out, and_3_out, and_4_out, and_5_out, and_6_out, and_7_out, decoder_1_out_0,
       decoder_1_out_1, decoder_1_out_2, decoder_1_out_3, decoder_1_out_4, decoder_1_out_5, decoder_1_out_6,
       decoder_1_out_7;
  wire [3:0] R1_q, R2_q, R3_q, R4_q, R5_q, R6_q, R7_q;

  Decoder #(.Selector_Bits(3)) decoder_1 (
    .sel(WriteReg), .out_0(decoder_1_out_0), .out_1(decoder_1_out_1), .out_2(decoder_1_out_2),
    .out_3(decoder_1_out_3), .out_4(decoder_1_out_4), .out_5(decoder_1_out_5), .out_6(decoder_1_out_6),
    .out_7(decoder_1_out_7));
  LED led_1 (.in(decoder_1_out_0));
  and and_1 (and_1_out, decoder_1_out_1, RegWrite);
  and and_2 (and_2_out, decoder_1_out_2, RegWrite);
  and and_3 (and_3_out, decoder_1_out_3, RegWrite);
  and and_4 (and_4_out, decoder_1_out_4, RegWrite);
  and and_5 (and_5_out, decoder_1_out_5, RegWrite);
  and and_6 (and_6_out, decoder_1_out_6, RegWrite);
  and and_7 (and_7_out, decoder_1_out_7, RegWrite);
  Register #(.Bits(4)) R1 (.D(WriteData), .C(Clock), .en(and_1_out), .Q(R1_q));
  Register #(.Bits(4)) R2 (.D(WriteData), .C(Clock), .en(and_2_out), .Q(R2_q));
  Register #(.Bits(4)) R3 (.D(WriteData), .C(Clock), .en(and_3_out), .Q(R3_q));
  Register #(.Bits(4)) R4 (.D(WriteData), .C(Clock), .en(and_4_out), .Q(R4_q));
  Register #(.Bits(4)) R5 (.D(WriteData), .C(Clock), .en(and_5_out), .Q(R5_q));
  Register #(.Bits(4)) R6 (.D(WriteData), .C(Clock), .en(and_6_out), .Q(R6_q));
  Register #(.Bits(4)) R7 (.D(WriteData), .C(Clock), .en(and_7_out), .Q(R7_q));
  Multiplexer #(.Selector_Bits(3), .Bits(4)) multiplexer_1 (
    .sel(ReadReg1), .in_0(4'b0000), .in_1(R1_q), .in_2(R2_q), .in_3(R3_q), .in_4(R4_q), .in_5(R5_q),
    .in_6(R6_q), .in_7(R7_q), .out(ReadData1));
  Multiplexer #(.Selector_Bits(3), .Bits(4)) multiplexer_2 (
    .sel(ReadReg2), .in_0(4'b0000), .in_1(R1_q), .in_2(R2_q), .in_3(R3_q), .in_4(R4_q), .in_5(R5_q),
    .in_6(R6_q), .in_7(R7_q), .out(ReadData2));
endmodule
